# Fritzing sketch Sketsa (saved by Fritzing 0.9.2b)
breadboards: 1

parts:
  Part1 = Arduino Leonardo (Rev3b)
  VCC1 = Battery block 9V
  Part2 = SRF05 Ultrasonic Rangefinder
  Part3 = Arduino Uno (Rev3)
  IC1 = L293D [package=THT]
  M1 = DC Motor
  M2 = DC Motor
  J1 = Basic Servo
  VCC2 = Battery block 9V

nets:
  VCC: Part1.5V, Part2.VCC, Part2.Trig, IC1.Enable_1, IC1.Enable_2, J1.vcc
  GND: Part1.GND, VCC1.-, Part2.GND, Part3.GND, IC1.0V, J1.gnd
  N1: Part1.VIN, VCC1.+
  N2: Part1.D10_PWM/A10, J1.pulse
  N3: Part3.D3_PWM, IC1.In_1
  N4: Part3.D4, IC1.In_2
  N5: Part3.5V, IC1.+Vmotor
  N6: Part3.VIN, VCC2.+
  N7: IC1.Out_1_(_Controlled_by_Enable_1_), M2.pin_2
  N8: IC1.Out_2_(_Controlled_by_Enable_1_), M2.pin_1
  N9: IC1.Out_3_(_Controlled_by_Enable_2_), M1.pin_2
  N10: IC1.In_4, M1.pin_1
